// Logisim project FinalQ5.circ as structural Verilog: 1 circuit, main circuit main
module main (
  input  RESET,
  output [1:0] out_2
);

  wire and_2_out, CLK_out, d_ff_1_q, d_ff_1_qn, d_ff_2_qn, not_1_out, not_2_out;

  Clock CLK (.out(CLK_out));
  D_Flip_Flop d_ff_1 (.D(out_2[0]), .clk(CLK_out), .Q(d_ff_1_q), .Qn(d_ff_1_qn), .reset(RESET));  // open: preset
  not not_1 (not_1_out, RESET);
  and and_1 (out_2[0], d_ff_1_qn, not_1_out);
  D_Flip_Flop d_ff_2 (.D(and_2_out), .clk(d_ff_1_q), .Q(out_2[1]), .Qn(d_ff_2_qn), .reset(RESET));  // open: preset
  and and_2 (and_2_out, d_ff_2_qn, not_2_out);
  not not_2 (not_2_out, RESET);
endmodule
