// Logisim project FinalQ6.circ as structural Verilog: 1 circuit, main circuit main
module main (
  input  REQ,
  input  DONE,
  input  RESET,
  output GO,
  output ACK
);

  wire CLK_out, d_ff_1_q, d_ff_2_qn, not_1_out, xor_1_out;

  Clock CLK (.out(CLK_out));
  D_Flip_Flop d_ff_1 (.D(REQ), .clk(CLK_out), .Q(d_ff_1_q), .reset(RESET));  // open: Qn, preset
  D_Flip_Flop d_ff_2 (.D(d_ff_2_qn), .clk(DONE), .Q(ACK), .Qn(d_ff_2_qn), .reset(RESET));  // open: preset
  xor xor_1 (xor_1_out, REQ, d_ff_1_q);
  not not_1 (not_1_out, DONE);
  and and_1 (GO, xor_1_out, not_1_out);
endmodule
