// Logisim project FinalQ8.circ as structural Verilog: 1 circuit, main circuit main
module main (
  input  RESET,
  input  GO,
  input  [7:0] N,
  output [3:0] Q,
  output [5:0] R,
  output DONE
);

  wire and_1_out, and_2_out, CLK_out, comparator_1_eq, comparator_1_lt, d_ff_1_q, d_ff_2_qn, d_ff_3_qn,
       not_1_out, not_2_out, not_3_out, or_1_out, or_2_out, xor_1_out;
  wire [1:0] d_ff_2_q, multiplexer_1_out, multiplexer_2_out;
  wire [3:0] sqrt_register_q;
  wire [5:0] adder_1_out, adder_2_out, adder_3_out, bit_extender_1_out, bit_extender_2_out,
       Remainder_register_q, shifter_1_out, shifter_2_out, shifter_3_out, subtractor_1_out;

  Clock CLK (.out(CLK_out));
  D_Flip_Flop d_ff_1 (.D(GO), .clk(CLK_out), .Q(d_ff_1_q));  // open: Qn, preset, reset
  xor xor_1 (xor_1_out, GO, d_ff_1_q);
  Multiplexer #(.select(2), .width(2)) multiplexer_1 (
    .in0(N[7:6]), .in1(N[5:4]), .in2(N[3:2]), .in3(N[1:0]), .out(multiplexer_1_out), .sel(d_ff_2_q));
  and and_1 (and_1_out, GO, xor_1_out);
  or or_1 (or_1_out, RESET, and_1_out);
  Register #(.width(4)) sqrt_register (.D(Q), .en(not_1_out), .clk(CLK_out), .Q(sqrt_register_q), .clr(or_1_out));
  not not_1 (not_1_out, DONE);
  Register #(.width(6)) Remainder_register (
    .D(R), .en(not_2_out), .clk(CLK_out), .Q(Remainder_register_q), .clr(or_1_out));
  not not_2 (not_2_out, DONE);
  assign bit_extender_1_out = {{4{1'b0}}, multiplexer_1_out};  // Bit_Extender bit_extender_1
  assign bit_extender_2_out = {{2{1'b0}}, sqrt_register_q};  // Bit_Extender bit_extender_2
  Shifter #(.width(6)) shifter_1 (.in(Remainder_register_q), .\dist (3'b010), .out(shifter_1_out));
  D_Flip_Flop d_ff_2 (
    .D(d_ff_2_qn), .clk(and_2_out), .Q(d_ff_2_q[0]), .Qn(d_ff_2_qn), .reset(or_1_out));  // open: preset
  not not_3 (not_3_out, DONE);
  and and_2 (and_2_out, not_3_out, CLK_out);
  Shifter #(.width(6)) shifter_2 (.in(bit_extender_2_out), .\dist (3'b010), .out(shifter_2_out));
  Adder #(.width(6)) adder_1 (.a(shifter_2_out), .b(6'b000001), .out(adder_1_out));  // open: cin, cout
  Adder #(.width(6)) adder_2 (.a(shifter_1_out), .b(bit_extender_1_out), .out(adder_2_out));  // open: cin, cout
  D_Flip_Flop d_ff_3 (
    .D(d_ff_3_qn), .clk(d_ff_2_qn), .Q(d_ff_2_q[1]), .Qn(d_ff_3_qn), .reset(or_1_out));  // open: preset
  Shifter #(.width(6)) shifter_3 (.in(bit_extender_2_out), .\dist (3'b001), .out(shifter_3_out));
  Comparator #(.mode("unsigned"), .width(6)) comparator_1 (
    .a(adder_1_out), .b(adder_2_out), .eq(comparator_1_eq), .lt(comparator_1_lt));  // open: gt
  Multiplexer #(.width(6)) multiplexer_2 (
    .in0(shifter_3_out), .in1(adder_3_out), .out({multiplexer_2_out, Q}), .sel(or_2_out));
  Adder #(.width(6)) adder_3 (.a(shifter_3_out), .b(6'b000001), .out(adder_3_out));  // open: cin, cout
  or or_2 (or_2_out, comparator_1_eq, comparator_1_lt);
  Comparator #(.mode("unsigned"), .width(2)) comparator_2 (.a(2'b11), .b(d_ff_2_q), .eq(DONE));  // open: gt, lt
  Subtractor #(.width(6)) subtractor_1 (.a(adder_2_out), .b(adder_1_out), .out(subtractor_1_out));  // open: bin, bout
  Multiplexer #(.width(6)) multiplexer_3 (.in0(adder_2_out), .in1(subtractor_1_out), .out(R), .sel(or_2_out));

  // Notes on the sheet:
  //   Counter
endmodule
