// Logisim project FinalQ3.circ as structural Verilog: 1 circuit, main circuit main
module main (
  input  [7:0] i,
  input  [1:0] C,
  output [1:0] a
);

  wire and_1_out, and_2_out, and_3_out, and_4_out, and_5_out, and_6_out, and_7_out, and_8_out, and_9_out,
       and_10_out, and_11_out, and_12_out, not_1_out, not_2_out, not_3_out, not_4_out, not_5_out, not_6_out,
       or_1_out, or_2_out, or_3_out, or_4_out;

  not not_1 (not_1_out, C[0]);
  not not_2 (not_2_out, C[0]);
  not not_3 (not_3_out, C[0]);
  not not_4 (not_4_out, C[0]);
  and and_1 (and_1_out, C[0], i[5]);
  and and_2 (and_2_out, not_1_out, i[7]);
  and and_3 (and_3_out, C[0], i[1]);
  and and_4 (and_4_out, not_2_out, i[3]);
  and and_5 (and_5_out, C[0], i[4]);
  and and_6 (and_6_out, not_3_out, i[6]);
  and and_7 (and_7_out, C[0], i[0]);
  and and_8 (and_8_out, not_4_out, i[2]);
  not not_5 (not_5_out, C[1]);
  or or_1 (or_1_out, and_1_out, and_2_out);
  or or_2 (or_2_out, and_3_out, and_4_out);
  not not_6 (not_6_out, C[1]);
  or or_3 (or_3_out, and_5_out, and_6_out);
  or or_4 (or_4_out, and_7_out, and_8_out);
  and and_9 (and_9_out, not_5_out, or_1_out);
  and and_10 (and_10_out, C[1], or_2_out);
  and and_11 (and_11_out, not_6_out, or_3_out);
  and and_12 (and_12_out, C[1], or_4_out);
  or or_5 (a[1], and_9_out, and_10_out);
  or or_6 (a[0], and_11_out, and_12_out);
endmodule
