// Logisim project FinalQ7.circ as structural Verilog: 1 circuit, main circuit main
module main (
  input  REQ,
  input  DONE,
  input  RESET,
  output GO,
  output ACK
);

  wire d_ff_1_q, d_ff_2_qn;

  Clock CLK ();  // open: out
  D_Flip_Flop d_ff_1 (.D(REQ), .clk(DONE), .Q(d_ff_1_q), .reset(RESET));  // open: Qn, preset
  D_Flip_Flop d_ff_2 (.D(d_ff_2_qn), .clk(DONE), .Q(ACK), .Qn(d_ff_2_qn), .reset(RESET));  // open: preset
  xor xor_1 (GO, REQ, d_ff_1_q);
endmodule
