// Logisim project HW2.circ as structural Verilog: 8 circuits, main circuit main
module main (
);

  // AND_Gate and_1 is placed but not wired
endmodule

module Problem1 (
  input  A,
  input  B,
  input  C,
  input  A_2,
  input  B_2,
  input  C_2,
  output Y,
  output out_8
);

  wire and_1_out, and_2_out, and_3_out, and_4_out, and_5_out, not_1_out, not_2_out;

  and and_1 (and_1_out, A_2, B_2);
  and and_2 (and_2_out, C_2, B_2, not_1_out);
  not not_1 (not_1_out, A_2);
  nor nor_1 (out_8, and_1_out, and_2_out);
  and and_3 (and_3_out, A, B);
  and and_4 (and_4_out, B, C);
  and and_5 (and_5_out, C, B, not_2_out);
  not not_2 (not_2_out, A);
  nor nor_2 (Y, and_3_out, and_4_out, and_5_out);

  // Notes on the sheet:
  //   Original Circuit
endmodule

module Problem2q2 (
  input  M3,
  input  M2,
  input  M1,
  input  M0,
  output q2
);

  wire and_1_out, and_2_out, not_1_out, not_2_out;

  not not_1 (not_1_out, M2);
  not not_2 (not_2_out, M0);
  and and_1 (and_1_out, not_1_out, not_2_out);
  and and_2 (and_2_out, not_2_out, M1);
  or or_1 (q2, and_1_out, and_2_out);
endmodule

module Problem2 (
  input  M3,
  input  M2,
  input  M1,
  input  M0,
  output q5,
  output q2
);

  wire and_1_out, and_2_out, and_3_out, and_4_out, not_1_out, not_2_out, not_3_out;

  not not_1 (not_1_out, M2);
  not not_2 (not_2_out, M1);
  not not_3 (not_3_out, M0);
  and and_1 (and_1_out, not_2_out, not_3_out);
  and and_2 (and_2_out, M1, M0);
  and and_3 (and_3_out, not_1_out, not_3_out);
  and and_4 (and_4_out, M1, not_3_out);
  or or_1 (q5, not_1_out, and_1_out, and_2_out);
  or or_2 (q2, and_3_out, and_4_out);
endmodule

module Problem3 (
  input  [5:0] in_1,
  output [15:0] out_2,
  output [15:0] out_3,
  output [15:0] out_4,
  output [15:0] out_5,
  output [15:0] out_6
);

  wire [15:0] decoder_1_out0;

  Demultiplexer #(.select(2), .width(16)) demultiplexer_1 (
    .out0(out_2), .out1(out_3), .out2(out_5), .out3(out_6), .in(decoder_1_out0), .sel(in_1[5:4]));
  Decoder #(.select(4)) decoder_1 (
    .out0(decoder_1_out0[0]), .out1(decoder_1_out0[1]), .out2(decoder_1_out0[2]), .out3(decoder_1_out0[3]),
    .out4(decoder_1_out0[4]), .out5(decoder_1_out0[5]), .out6(decoder_1_out0[6]), .out7(decoder_1_out0[7]),
    .out8(decoder_1_out0[8]), .out9(decoder_1_out0[9]), .out10(decoder_1_out0[10]),
    .out11(decoder_1_out0[11]), .out12(decoder_1_out0[12]), .out13(decoder_1_out0[13]),
    .out14(decoder_1_out0[14]), .out15(decoder_1_out0[15]), .sel(in_1[3:0]), .en(1'b1));

  assign out_4 = out_3;

  // Notes on the sheet:
  //   A[5:0]
  //   X0
  //   X1
  //   X2
  //   X3
endmodule

module Problem4 (
  input  [3:0] in_1,
  input  [3:0] in_2,
  input  [3:0] in_3,
  output [3:0] out_4
);

  wire and_1_out, and_2_out, and_3_out, comparator_1_eq, comparator_1_gt, comparator_2_eq, comparator_2_gt,
       comparator_3_eq, comparator_3_gt, nor_1_out, not_1_out, not_2_out, or_1_out, or_2_out, or_3_out;
  wire [1:0] or_4_out;

  or or_1 (or_1_out, comparator_1_gt, comparator_1_eq);
  Comparator #(.mode("unsigned"), .width(4)) comparator_1 (
    .a(in_1), .b(in_2), .gt(comparator_1_gt), .eq(comparator_1_eq));  // open: lt
  or or_2 (or_2_out, comparator_2_gt, comparator_2_eq);
  Comparator #(.mode("unsigned"), .width(4)) comparator_2 (
    .a(in_1), .b(in_3), .gt(comparator_2_gt), .eq(comparator_2_eq));  // open: lt
  or or_3 (or_3_out, comparator_3_gt, comparator_3_eq);
  Comparator #(.mode("unsigned"), .width(4)) comparator_3 (
    .a(in_2), .b(in_3), .gt(comparator_3_gt), .eq(comparator_3_eq));  // open: lt
  not not_1 (not_1_out, or_2_out);
  not not_2 (not_2_out, or_3_out);
  and and_1 (and_1_out, or_1_out, or_3_out);
  nor nor_1 (nor_1_out, or_1_out, or_3_out);
  and and_2 (and_2_out, not_1_out, or_3_out);
  and and_3 (and_3_out, or_2_out, not_2_out);
  or or_4 (or_4_out[0], and_1_out, nor_1_out);
  or or_5 (or_4_out[1], and_2_out, and_3_out);
  Multiplexer #(.select(2), .width(4)) multiplexer_1 (
    .in0(in_1), .in1(in_2), .in2(in_3), .out(out_4), .sel(or_4_out));  // open: in3

  // Notes on the sheet:
  //   A
  //   B
  //   C
  //   A >= B
  //   A >= C
  //   B >= C
endmodule

module Problem5 (
  input  [4:0] P,
  input  [4:0] K,
  output [4:0] C
);

  wire adder_1_cout, comparator_1_gt, or_1_out;
  wire [4:0] adder_1_out, subtractor_1_out;

  Adder #(.width(5)) adder_1 (.a(P), .b(K), .out(adder_1_out), .cout(adder_1_cout));  // open: cin
  Subtractor #(.width(5)) subtractor_1 (.a(adder_1_out), .b(5'b11001), .out(subtractor_1_out));  // open: bin, bout
  Comparator #(.mode("unsigned"), .width(5)) comparator_1 (
    .a(adder_1_out), .b(5'b11001), .gt(comparator_1_gt));  // open: eq, lt
  Multiplexer #(.width(5)) multiplexer_1 (.in0(adder_1_out), .in1(subtractor_1_out), .out(C), .sel(or_1_out));
  or or_1 (or_1_out, comparator_1_gt, adder_1_cout);
endmodule

module Problem6 (
  input  [3:0] in_1,
  input  [3:0] in_2,
  output [6:0] Z
);

  wire [6:0] adder_1_out, bit_extender_1_out, bit_extender_2_out, shifter_1_out, shifter_2_out;

  assign bit_extender_1_out = {{3{1'b0}}, in_1};  // Bit_Extender bit_extender_1
  assign bit_extender_2_out = {{3{1'b0}}, in_2};  // Bit_Extender bit_extender_2
  Shifter #(.width(7)) shifter_1 (.in(bit_extender_1_out), .\dist (3'b011), .out(shifter_1_out));
  Shifter #(.width(7)) shifter_2 (.in(bit_extender_1_out), .\dist (3'b001), .out(shifter_2_out));
  Adder #(.width(7)) adder_1 (.a(shifter_1_out), .b(shifter_2_out), .out(adder_1_out));  // open: cin, cout
  Adder #(.width(7)) adder_2 (.a(adder_1_out), .b(bit_extender_2_out), .out(Z));  // open: cin, cout

  // Notes on the sheet:
  //   D1
  //   D0
endmodule
