// Logisim project HW1Q7.circ as structural Verilog: 1 circuit, main circuit Test
module Test (
  input  [3:0] M,
  output Y
);

  wire nor_1_out, nor_2_out, nor_3_out, not_1_out, not_2_out;

  not not_1 (not_1_out, M[0]);
  not not_2 (not_2_out, M[3]);
  nor nor_1 (nor_1_out, M[3], not_1_out);
  nor nor_2 (nor_2_out, not_2_out, M[0]);
  nor nor_3 (nor_3_out, nor_1_out, nor_2_out);
  not not_3 (Y, nor_3_out);
endmodule
