// Logisim project HW2Q3.circ as structural Verilog: 1 circuit, main circuit main
module main (
  input  [5:0] A,
  output [15:0] X0,
  output [15:0] X1,
  output [15:0] X2,
  output [15:0] X3
);

  wire [15:0] decoder_1_out0;

  Demultiplexer #(.select(2), .width(16)) demultiplexer_1 (
    .out0(X0), .out1(X1), .out2(X2), .out3(X3), .in(decoder_1_out0), .sel(A[5:4]));
  Decoder #(.select(4)) decoder_1 (
    .out0(decoder_1_out0[0]), .out1(decoder_1_out0[1]), .out2(decoder_1_out0[2]), .out3(decoder_1_out0[3]),
    .out4(decoder_1_out0[4]), .out5(decoder_1_out0[5]), .out6(decoder_1_out0[6]), .out7(decoder_1_out0[7]),
    .out8(decoder_1_out0[8]), .out9(decoder_1_out0[9]), .out10(decoder_1_out0[10]),
    .out11(decoder_1_out0[11]), .out12(decoder_1_out0[12]), .out13(decoder_1_out0[13]),
    .out14(decoder_1_out0[14]), .out15(decoder_1_out0[15]), .sel(A[3:0]));  // open: en

  // Notes on the sheet:
  //   A[5:0]
endmodule
