// Logisim project HW2Q4.circ as structural Verilog: 1 circuit, main circuit main
module main (
  input  [3:0] A,
  input  [3:0] B,
  input  [3:0] C,
  output [3:0] M
);

  wire and_1_out, and_2_out, and_3_out, comparator_1_eq, comparator_1_gt, comparator_2_eq, comparator_2_gt,
       comparator_3_eq, comparator_3_gt, nor_1_out, not_1_out, not_2_out, or_1_out, or_2_out, or_3_out;
  wire [1:0] or_4_out;

  or or_1 (or_1_out, comparator_1_gt, comparator_1_eq);
  Comparator #(.mode("unsigned"), .width(4)) comparator_1 (
    .a(A), .b(B), .gt(comparator_1_gt), .eq(comparator_1_eq));  // open: lt
  or or_2 (or_2_out, comparator_2_gt, comparator_2_eq);
  Comparator #(.mode("unsigned"), .width(4)) comparator_2 (
    .a(A), .b(C), .gt(comparator_2_gt), .eq(comparator_2_eq));  // open: lt
  or or_3 (or_3_out, comparator_3_gt, comparator_3_eq);
  Comparator #(.mode("unsigned"), .width(4)) comparator_3 (
    .a(B), .b(C), .gt(comparator_3_gt), .eq(comparator_3_eq));  // open: lt
  not not_1 (not_1_out, or_2_out);
  not not_2 (not_2_out, or_3_out);
  and and_1 (and_1_out, or_1_out, or_3_out);
  nor nor_1 (nor_1_out, or_1_out, or_3_out);
  and and_2 (and_2_out, not_1_out, or_3_out);
  and and_3 (and_3_out, or_2_out, not_2_out);
  or or_4 (or_4_out[0], and_1_out, nor_1_out);
  or or_5 (or_4_out[1], and_2_out, and_3_out);
  Multiplexer #(.select(2), .width(4)) multiplexer_1 (.in0(A), .in1(B), .in2(C), .out(M), .sel(or_4_out));  // open: in3

  // Notes on the sheet:
  //   A >= B
  //   A >= C
  //   B >= C
endmodule
