// Logisim project HW2Q5.circ as structural Verilog: 1 circuit, main circuit main
module main (
  input  [4:0] P,
  input  [4:0] K,
  output [4:0] C
);

  wire adder_1_cout, comparator_1_eq, comparator_1_gt, or_1_out;
  wire [4:0] adder_1_out, subtractor_1_out;

  Adder #(.width(5)) adder_1 (.a(P), .b(K), .out(adder_1_out), .cout(adder_1_cout));  // open: cin
  Subtractor #(.width(5)) subtractor_1 (.a(adder_1_out), .b(5'b11010), .out(subtractor_1_out));  // open: bin, bout
  Comparator #(.mode("unsigned"), .width(5)) comparator_1 (
    .a(adder_1_out), .b(5'b11010), .gt(comparator_1_gt), .eq(comparator_1_eq));  // open: lt
  Multiplexer #(.width(5)) multiplexer_1 (.in0(adder_1_out), .in1(subtractor_1_out), .out(C), .sel(or_1_out));
  or or_1 (or_1_out, comparator_1_gt, comparator_1_eq, adder_1_cout);
endmodule
