// Logisim project problem7.circ as structural Verilog: 3 circuits, main circuit main
module main (
);

  // NOR_Gate nor_1 is placed but not wired
endmodule

module Test (
  input  M3,
  input  M2,
  input  M1,
  input  M0,
  output Y
);

  wire nor_1_out, nor_2_out, nor_3_out, not_1_out, not_2_out;

  not not_1 (not_1_out, M0);
  not not_2 (not_2_out, M3);
  nor nor_1 (nor_1_out, M3, not_1_out);
  nor nor_2 (nor_2_out, not_2_out, M0);
  nor nor_3 (nor_3_out, nor_1_out, nor_2_out);
  not not_3 (Y, nor_3_out);
endmodule

module test2 (
  input  M3,
  input  M2,
  input  M1,
  input  M0,
  output Y
);

  wire nand_1_out, nand_2_out, nand_3_out, nand_4_out;

  nand nand_1 (nand_1_out, 1'b1, M3);
  nand nand_2 (nand_2_out, 1'b1, M0);
  nand nand_3 (nand_3_out, nand_1_out, M0);
  nand nand_4 (nand_4_out, M3, nand_2_out);
  nand nand_5 (Y, nand_3_out, nand_4_out);
endmodule
