// Logisim project HW3Q3.circ as structural Verilog: 2 circuits, main circuit main
module main (
  input  X,
  input  RESET,
  output Y_1,
  output Y_0
);

  wire and_1_out, and_2_out, and_3_out, CLK_out, d_ff_1_qn, d_ff_2_qn, or_1_out;

  Clock CLK (.out(CLK_out));
  and and_1 (and_1_out, Y_0, X);
  and and_2 (and_2_out, d_ff_2_qn, Y_1);
  or or_1 (or_1_out, and_1_out, and_2_out);
  and and_3 (and_3_out, d_ff_1_qn, X);
  D_Flip_Flop d_ff_1 (.D(or_1_out), .clk(CLK_out), .Q(Y_1), .Qn(d_ff_1_qn), .reset(RESET));  // open: preset
  D_Flip_Flop d_ff_2 (.D(and_3_out), .clk(CLK_out), .Q(Y_0), .Qn(d_ff_2_qn), .reset(RESET));  // open: preset
endmodule

module OtherMethdo (
  input  X,
  input  RESET,
  output Y_1,
  output Y_0
);

  wire and_1_out, and_2_out, and_3_out, and_4_out, CLK_out, d_ff_2_qn, or_1_out, or_2_out;

  Clock CLK (.out(CLK_out));
  and and_1 (and_1_out, Y_1, Y_0);
  and and_2 (and_2_out, Y_1, X);
  and and_3 (and_3_out, X, Y_0);
  and and_4 (and_4_out, X, d_ff_2_qn);
  or or_1 (or_1_out, and_1_out, and_2_out, and_3_out);
  or or_2 (or_2_out, and_1_out, and_4_out);
  D_Flip_Flop d_ff_1 (.D(or_1_out), .clk(CLK_out), .Q(Y_1), .reset(RESET));  // open: Qn, preset
  D_Flip_Flop d_ff_2 (.D(or_2_out), .clk(CLK_out), .Q(Y_0), .Qn(d_ff_2_qn), .reset(RESET));  // open: preset
endmodule
