// Logisim project HW3Q4.circ as structural Verilog: 1 circuit, main circuit main
module main (
  input  DIN,
  input  RESET,
  output DOUT
);

  wire CLK_out, d_ff_1_q, d_ff_2_q, d_ff_3_q, xor_1_out;

  Clock CLK (.out(CLK_out));
  D_Flip_Flop d_ff_1 (.D(DIN), .clk(CLK_out), .Q(d_ff_1_q), .reset(RESET));  // open: Qn, preset
  D_Flip_Flop d_ff_2 (.D(DIN), .clk(CLK_out), .Q(d_ff_2_q), .reset(RESET));  // open: Qn, preset
  D_Flip_Flop d_ff_3 (.D(d_ff_1_q), .clk(CLK_out), .Q(d_ff_3_q), .reset(RESET));  // open: Qn, preset
  xor xor_1 (xor_1_out, d_ff_2_q, d_ff_3_q);
  and and_1 (DOUT, d_ff_2_q, xor_1_out);
endmodule
