// Logisim project HW3Q5.circ as structural Verilog: 1 circuit, main circuit main
module main (
  input  DIN,
  output DOUT_SHORT,
  output DOUT_LONG
);

  wire and_1_out, CLK_out, d_ff_1_q, d_ff_2_q, d_ff_3_q, d_ff_4_q, d_ff_5_q, d_ff_6_q, d_ff_7_q, not_1_out,
       xor_1_out;

  Clock CLK (.out(CLK_out));
  D_Flip_Flop d_ff_1 (.D(DIN), .clk(CLK_out), .Q(d_ff_1_q));  // open: Qn, preset, reset
  D_Flip_Flop d_ff_2 (.D(DIN), .clk(CLK_out), .Q(d_ff_2_q));  // open: Qn, preset, reset
  D_Flip_Flop d_ff_3 (.D(DIN), .clk(CLK_out), .Q(d_ff_3_q));  // open: Qn, preset, reset
  D_Flip_Flop d_ff_4 (.D(d_ff_2_q), .clk(CLK_out), .Q(d_ff_4_q));  // open: Qn, preset, reset
  D_Flip_Flop d_ff_5 (.D(d_ff_1_q), .clk(CLK_out), .Q(d_ff_5_q));  // open: Qn, preset, reset
  D_Flip_Flop d_ff_6 (.D(d_ff_4_q), .clk(CLK_out), .Q(d_ff_6_q));  // open: Qn, preset, reset
  D_Flip_Flop d_ff_7 (.D(d_ff_6_q), .clk(CLK_out), .Q(d_ff_7_q));  // open: Qn, preset, reset
  xor xor_1 (xor_1_out, d_ff_3_q, d_ff_5_q);
  not not_1 (not_1_out, d_ff_3_q);
  and and_1 (and_1_out, not_1_out, xor_1_out);
  Demultiplexer demultiplexer_1 (.out0(DOUT_SHORT), .out1(DOUT_LONG), .in(and_1_out), .sel(d_ff_7_q));
endmodule
