// Logisim project HW3Q6.circ as structural Verilog: 1 circuit, main circuit main
module main (
  input  RESET,
  input  DIN,
  output DOUT
);

  wire CLK_out, d_ff_1_q;
  wire [2:0] divider_1_rem, Remainder_q;
  wire [3:0] adder_1_out, bit_extender_1_out, bit_extender_2_out, multiplier_1_out;
  wire [3:3] divider_1_rem_2;

  Register #(.width(3)) Remainder (.D(divider_1_rem), .clk(CLK_out), .Q(Remainder_q), .clr(RESET));  // open: en
  Clock CLK (.out(CLK_out));
  D_Flip_Flop d_ff_1 (.D(DIN), .clk(CLK_out), .Q(d_ff_1_q), .reset(RESET));  // open: Qn, preset
  assign bit_extender_1_out = {{1{1'b0}}, Remainder_q};  // Bit_Extender bit_extender_1
  assign bit_extender_2_out = {{3{1'b0}}, d_ff_1_q};  // Bit_Extender bit_extender_2
  Multiplier #(.width(4)) multiplier_1 (
    .a(bit_extender_1_out), .b(4'b0010), .out(multiplier_1_out));  // open: cin, cout
  Adder #(.width(4)) adder_1 (.a(multiplier_1_out), .b(bit_extender_2_out), .out(adder_1_out));  // open: cin, cout
  Divider #(.width(4)) divider_1 (
    .a(adder_1_out), .b(4'b0110), .rem({divider_1_rem_2[3], divider_1_rem}));  // open: out, upper
  nor nor_1 (DOUT, divider_1_rem[0], divider_1_rem[1], divider_1_rem[2]);
endmodule
