// Logisim project HW4Q5.circ as structural Verilog: 1 circuit, main circuit main
module main (
  input  [7:0] A,
  input  [7:0] D,
  input  REQ,
  input  RST,
  output [7:0] R,
  output [7:0] Q,
  output ACK
);

  wire clk_out, d_ff_1_q, d_ff_2_q, d_ff_2_qn, d_ff_3_q, Falling_edge_detector_out, not_1_out, not_2_out,
       not_3_out, or_1_out, or_2_out, Rising_edge_detector_out, subtractor_1_bout, xor_1_out;
  wire [7:0] counter_1_q;
  wire [15:0] adder_1_out, adder_2_out, bit_extender_1_out, bit_extender_2_out, bit_extender_3_out,
       Divisor_register_q, multiplexer_1_out, multiplexer_2_out, multiplexer_3_out, multiplexer_4_out,
       shifter_1_out, shifter_2_out, shifter_3_out, subtractor_1_out;
  wire [15:8] Quotient_register_q, Remainder_register_q;

  D_Flip_Flop d_ff_1 (.D(REQ), .clk(clk_out), .Q(d_ff_1_q), .reset(RST));  // open: Qn, preset
  Clock clk (.out(clk_out));
  D_Flip_Flop d_ff_2 (.D(REQ), .clk(clk_out), .Q(d_ff_2_q), .Qn(d_ff_2_qn), .reset(RST));  // open: preset
  D_Flip_Flop d_ff_3 (.D(d_ff_1_q), .clk(clk_out), .Q(d_ff_3_q), .reset(RST));  // open: Qn, preset
  xor xor_1 (xor_1_out, d_ff_2_q, d_ff_3_q);
  assign bit_extender_1_out = {{8{1'b0}}, A};  // Bit_Extender bit_extender_1
  assign bit_extender_2_out = {{8{1'b0}}, D};  // Bit_Extender bit_extender_2
  and Rising_edge_detector (Rising_edge_detector_out, d_ff_2_q, xor_1_out);
  and Falling_edge_detector (Falling_edge_detector_out, xor_1_out, d_ff_2_qn);
  Multiplexer #(.width(16)) multiplexer_1 (
    .in0(multiplexer_4_out), .in1(bit_extender_1_out), .out(multiplexer_1_out), .sel(Rising_edge_detector_out));
  or or_1 (or_1_out, Falling_edge_detector_out, RST);
  Shifter #(.width(16)) shifter_1 (.in(bit_extender_2_out), .\dist (4'b1000), .out(shifter_1_out));
  Multiplexer #(.width(16)) multiplexer_2 (
    .in0(adder_2_out), .in1({16{1'b0}}), .out(multiplexer_2_out), .sel(Rising_edge_detector_out));
  Register #(.width(16)) Remainder_register (
    .D(multiplexer_1_out), .en(not_3_out), .clk(clk_out), .Q({Remainder_register_q, R}), .clr(or_1_out));
  Register #(.width(16)) Divisor_register (
    .D(multiplexer_3_out), .en(not_3_out), .clk(clk_out), .Q(Divisor_register_q), .clr(or_1_out));
  Multiplexer #(.width(16)) multiplexer_3 (
    .in0(shifter_2_out), .in1(shifter_1_out), .out(multiplexer_3_out), .sel(Rising_edge_detector_out));
  Register #(.width(16)) Quotient_register (
    .D(multiplexer_2_out), .en(not_3_out), .clk(clk_out), .Q({Quotient_register_q, Q}), .clr(or_1_out));
  Shifter #(.shift("lr"), .width(16)) shifter_2 (.in(Divisor_register_q), .\dist (4'b0001), .out(shifter_2_out));
  Shifter #(.width(16)) shifter_3 (.in({Quotient_register_q, Q}), .\dist (4'b0001), .out(shifter_3_out));
  Counter counter_1 (.count(not_1_out), .Q(counter_1_q), .clk(clk_out), .clr(or_2_out));  // open: load, D, carry, up
  not not_1 (not_1_out, ACK);
  or or_2 (or_2_out, Rising_edge_detector_out, or_1_out);
  Subtractor #(.width(16)) subtractor_1 (
    .a({Remainder_register_q, R}), .b(Divisor_register_q), .out(subtractor_1_out), .bout(subtractor_1_bout));  // open: bin
  Comparator comparator_1 (.a(counter_1_q), .b(8'h8), .gt(ACK));  // open: eq, lt
  Adder #(.width(16)) adder_1 (.a(subtractor_1_out), .b(Divisor_register_q), .out(adder_1_out));  // open: cin, cout
  not not_2 (not_2_out, subtractor_1_bout);
  Multiplexer #(.width(16)) multiplexer_4 (
    .in0(subtractor_1_out), .in1(adder_1_out), .out(multiplexer_4_out), .sel(subtractor_1_bout));
  assign bit_extender_3_out = {{15{1'b0}}, not_2_out};  // Bit_Extender bit_extender_3
  not not_3 (not_3_out, ACK);
  Adder #(.width(16)) adder_2 (.a(bit_extender_3_out), .b(shifter_3_out), .out(adder_2_out));  // open: cin, cout
endmodule
